// Logisim project Projeto MIPS.circ as structural Verilog: 12 circuits, main circuit main
module main (
  input  in_1
);

  wire and_1_out, CLK, ctrlunity_1_aluop0, ctrlunity_1_aluop1, ctrlunity_1_alusrc, ctrlunity_1_branch,
       ctrlunity_1_memread, ctrlunity_1_memtoreg, ctrlunity_1_memwrite, ctrlunity_1_regdst,
       ctrlunity_1_regwrite, ula_1_out_4;
  wire [2:0] aluctrl_1_out_4;
  wire [4:0] multiplexer_1_out;
  wire [31:0] adder_1_out, adder_2_out, bit_extender_1_out, memdata_1_dataout, meminstr_1_out_2,
       multiplexer_2_out, multiplexer_3_out, multiplexer_4_out, regbank_1_rd1, regbank_1_rd2, register_1_q,
       shift_left_2_1_out_2, ula_1_out_5;

  Register #(.width(32)) register_1 (.D(multiplexer_3_out), .Q(register_1_q), .clk(CLK), .clr(in_1));  // open: en
  Clock clock_1 (.out(CLK));
  Adder #(.width(32)) adder_1 (.a(32'h4), .b(register_1_q), .out(adder_1_out));  // open: cin, cout
  MemInstr meminstr_1 (.in_1(register_1_q), .out_2(meminstr_1_out_2));
  // Probe on meminstr_1_out_2
  Multiplexer #(.width(5), .enable("false")) multiplexer_1 (
    .in0(meminstr_1_out_2[20:16]), .in1(meminstr_1_out_2[15:11]), .out(multiplexer_1_out),
    .sel(ctrlunity_1_regdst));
  CtrlUnity ctrlunity_1 (
    .RegDst(ctrlunity_1_regdst), .ALUSrc(ctrlunity_1_alusrc), .MemToReg(ctrlunity_1_memtoreg),
    .RegWrite(ctrlunity_1_regwrite), .MemRead(ctrlunity_1_memread), .MemWrite(ctrlunity_1_memwrite),
    .Branch(ctrlunity_1_branch), .ALUOp1(ctrlunity_1_aluop1), .ALUOp0(ctrlunity_1_aluop0),
    .in_1(meminstr_1_out_2[31:26]));
  RegBank regbank_1 (
    .in_1(multiplexer_4_out), .CLK(CLK), .RegWrite(ctrlunity_1_regwrite), .W(multiplexer_1_out),
    .RR1(meminstr_1_out_2[25:21]), .RD1(regbank_1_rd1), .RR2(meminstr_1_out_2[20:16]), .RD2(regbank_1_rd2));
  assign bit_extender_1_out = {{16{meminstr_1_out_2[15]}}, meminstr_1_out_2[15:0]};  // Bit_Extender bit_extender_1
  Multiplexer #(.width(32), .enable("false")) multiplexer_2 (
    .in0(regbank_1_rd2), .in1(bit_extender_1_out), .out(multiplexer_2_out), .sel(ctrlunity_1_alusrc));
  ALUCtrl aluctrl_1 (
    .ALUOp1(ctrlunity_1_aluop1), .ALUOp0(ctrlunity_1_aluop0), .in_1(meminstr_1_out_2[15:0]),
    .out_4(aluctrl_1_out_4));
  Shift_Left_2 shift_left_2_1 (.in_1(bit_extender_1_out), .out_2(shift_left_2_1_out_2));
  ULA ula_1 (
    .A(regbank_1_rd1), .B(multiplexer_2_out), .in_3(aluctrl_1_out_4), .out_5(ula_1_out_5), .out_4(ula_1_out_4));
  Adder #(.width(32)) adder_2 (.a(adder_1_out), .b(shift_left_2_1_out_2), .out(adder_2_out));  // open: cin, cout
  MemData memdata_1 (
    .Addr(ula_1_out_5), .DataIn(regbank_1_rd2), .MemWrite(ctrlunity_1_memwrite), .CLK(CLK),
    .MemRead(ctrlunity_1_memread), .DataOut(memdata_1_dataout));
  and and_1 (and_1_out, ctrlunity_1_branch, ula_1_out_4);
  Multiplexer #(.width(32), .enable("false")) multiplexer_3 (
    .in0(adder_1_out), .in1(adder_2_out), .out(multiplexer_3_out), .sel(and_1_out));
  Multiplexer #(.width(32), .enable("false")) multiplexer_4 (
    .in0(memdata_1_dataout), .in1(ula_1_out_5), .out(multiplexer_4_out), .sel(ctrlunity_1_memtoreg));

  // Notes on the sheet:
  //   PCSrc
endmodule

module Type_R (
  input  [31:0] in_1,
  output [5:0] out_2,
  output [4:0] out_3,
  output [4:0] out_4,
  output [4:0] out_5,
  output [4:0] out_6,
  output [5:0] out_7
);


  assign out_2 = in_1[5:0];
  assign out_3 = in_1[10:6];
  assign out_4 = in_1[15:11];
  assign out_5 = in_1[20:16];
  assign out_6 = in_1[25:21];
  assign out_7 = in_1[31:26];
endmodule

module Type_I (
  input  [31:0] in_1,
  output [15:0] out_2,
  output [4:0] out_3,
  output [4:0] out_4,
  output [5:0] out_5
);


  assign out_2 = in_1[15:0];
  assign out_3 = in_1[20:16];
  assign out_4 = in_1[25:21];
  assign out_5 = in_1[31:26];
endmodule

module Type_J (
  input  [31:0] in_1,
  output [25:0] out_2,
  output [5:0] out_3
);


  assign out_2 = in_1[25:0];
  assign out_3 = in_1[31:26];
endmodule

module MemInstr (
  input  [31:0] in_1,
  output [31:0] out_2
);

  RAM #(.addrWidth(24)) ram_1 (.addr(in_1[25:2]), .data(out_2[31:24]));  // open: sel, clk, ld, clr
  RAM #(.addrWidth(24)) ram_2 (.addr(in_1[25:2]), .data(out_2[23:16]));  // open: sel, clk, ld, clr
  RAM #(.addrWidth(24)) ram_3 (.addr(in_1[25:2]), .data(out_2[15:8]));  // open: sel, clk, ld, clr
  RAM #(.addrWidth(24)) ram_4 (.addr(in_1[25:2]), .data(out_2[7:0]));  // open: sel, clk, ld, clr

  // Notes on the sheet:
  //   Descartados
endmodule

module RegBank (
  input  [31:0] in_1,
  input  CLK,
  input  [4:0] RR1,
  input  [4:0] RR2,
  input  RegWrite,
  input  [4:0] W,
  output [31:0] RD1,
  output [31:0] RD2
);

  wire EN1, EN2, EN3, EN4, EN5, EN6, EN7, EN8, EN9, EN10, EN11, EN12, EN13, EN14, EN15, EN16, EN17, EN18,
       EN19, EN20, EN21, EN22, EN23, EN24, EN25, EN26, EN27, EN28, EN29, EN30, EN31;
  wire [31:0] S1, S2, S3, S4, S5, S6, S7, S8, S9, S10, S11, S12, S13, S14, S15, S16, S17, S18, S19, S20, S21,
       S22, S23, S24, S25, S26, S27, S28, S29, S30, S31, undriven, undriven_2, undriven_3, undriven_4;

  Decoder #(.select(5)) decoder_1 (
    .out1(EN1), .out2(EN2), .out3(EN3), .out4(EN4), .out5(EN5), .out6(EN6), .out7(EN7), .out8(EN8),
    .out9(EN9), .out10(EN10), .out11(EN11), .out12(EN12), .out13(EN13), .out14(EN14), .out15(EN15),
    .out16(EN16), .out17(EN17), .out18(EN18), .out19(EN19), .out20(EN20), .out21(EN21), .out22(EN22),
    .out23(EN23), .out24(EN24), .out25(EN25), .out26(EN26), .out27(EN27), .out28(EN28), .out29(EN29),
    .out30(EN30), .out31(EN31), .sel(W), .en(RegWrite));  // open: out0
  Register #(.width(32)) register_1 (.D(in_1), .en(EN8), .Q(S8), .clk(CLK));  // open: clr
  Register #(.width(32)) register_2 (.D(in_1), .en(EN16), .Q(S16), .clk(CLK));  // open: clr
  Register #(.width(32)) register_3 (.D(in_1), .en(EN24), .Q(S24), .clk(CLK));  // open: clr
  Register #(.width(32)) register_4 (.D(in_1), .en(EN1), .Q(S1), .clk(CLK));  // open: clr
  Register #(.width(32)) register_5 (.D(in_1), .en(EN9), .Q(S9), .clk(CLK));  // open: clr
  Register #(.width(32)) register_6 (.D(in_1), .en(EN17), .Q(S17), .clk(CLK));  // open: clr
  Register #(.width(32)) register_7 (.D(in_1), .en(EN25), .Q(S25), .clk(CLK));  // open: clr
  Register #(.width(32)) register_8 (.D(in_1), .en(EN2), .Q(S2), .clk(CLK));  // open: clr
  Register #(.width(32)) register_9 (.D(in_1), .en(EN10), .Q(S10), .clk(CLK));  // open: clr
  Register #(.width(32)) register_10 (.D(in_1), .en(EN18), .Q(S18), .clk(CLK));  // open: clr
  Register #(.width(32)) register_11 (.D(in_1), .en(EN26), .Q(S26), .clk(CLK));  // open: clr
  Multiplexer #(.select(5), .width(32)) multiplexer_1 (
    .in0({32{1'b0}}), .in1(S1), .in2(S2), .in3(undriven), .in4(S4), .in5(S5), .in6(S6), .in7(undriven_2),
    .in8(S8), .in9(S9), .in10(S10), .in11(S11), .in12(S12), .in13(S13), .in14(S14), .in15(S15), .in16(S16),
    .in17(S17), .in18(S18), .in19(S19), .in20(S20), .in21(S21), .in22(S22), .in23(S23), .in24(S24),
    .in25(S25), .in26(S26), .in27(S27), .in28(S28), .in29(S29), .in30(S30), .in31(S31), .out(RD1), .sel(RR1));  // open: en
  Register #(.width(32)) register_12 (.D(in_1), .en(EN3), .Q(S3), .clk(CLK));  // open: clr
  Register #(.width(32)) register_13 (.D(in_1), .en(EN11), .Q(S11), .clk(CLK));  // open: clr
  Register #(.width(32)) register_14 (.D(in_1), .en(EN19), .Q(S19), .clk(CLK));  // open: clr
  Register #(.width(32)) register_15 (.D(in_1), .en(EN27), .Q(S27), .clk(CLK));  // open: clr
  Register #(.width(32)) register_16 (.D(in_1), .en(EN4), .Q(S4), .clk(CLK));  // open: clr
  Register #(.width(32)) register_17 (.D(in_1), .en(EN12), .Q(S12), .clk(CLK));  // open: clr
  Register #(.width(32)) register_18 (.D(in_1), .en(EN20), .Q(S20), .clk(CLK));  // open: clr
  Register #(.width(32)) register_19 (.D(in_1), .en(EN28), .Q(S28), .clk(CLK));  // open: clr
  Multiplexer #(.select(5), .width(32), .enable("false")) multiplexer_2 (
    .in0({32{1'b0}}), .in1(S1), .in2(S2), .in3(undriven_3), .in4(S4), .in5(S5), .in6(S6), .in7(undriven_4),
    .in8(S8), .in9(S9), .in10(S10), .in11(S11), .in12(S12), .in13(S13), .in14(S14), .in15(S15), .in16(S16),
    .in17(S17), .in18(S18), .in19(S19), .in20(S20), .in21(S21), .in22(S22), .in23(S23), .in24(S24),
    .in25(S25), .in26(S26), .in27(S27), .in28(S28), .in29(S29), .in30(S30), .in31(S31), .out(RD2), .sel(RR2));
  Register #(.width(32)) register_20 (.D(in_1), .en(EN5), .Q(S5), .clk(CLK));  // open: clr
  Register #(.width(32)) register_21 (.D(in_1), .en(EN13), .Q(S13), .clk(CLK));  // open: clr
  Register #(.width(32)) register_22 (.D(in_1), .en(EN21), .Q(S21), .clk(CLK));  // open: clr
  Register #(.width(32)) register_23 (.D(in_1), .en(EN29), .Q(S29), .clk(CLK));  // open: clr
  Register #(.width(32)) register_24 (.D(in_1), .en(EN6), .Q(S6), .clk(CLK));  // open: clr
  Register #(.width(32)) register_25 (.D(in_1), .en(EN14), .Q(S14), .clk(CLK));  // open: clr
  Register #(.width(32)) register_26 (.D(in_1), .en(EN22), .Q(S22), .clk(CLK));  // open: clr
  Register #(.width(32)) register_27 (.D(in_1), .en(EN30), .Q(S30), .clk(CLK));  // open: clr
  Register #(.width(32)) register_28 (.D(in_1), .en(EN7), .Q(S7), .clk(CLK));  // open: clr
  Register #(.width(32)) register_29 (.D(in_1), .en(EN15), .Q(S15), .clk(CLK));  // open: clr
  Register #(.width(32)) register_30 (.D(in_1), .en(EN23), .Q(S23), .clk(CLK));  // open: clr
  Register #(.width(32)) register_31 (.D(in_1), .en(EN31), .Q(S31), .clk(CLK));  // open: clr

  // Other names for the same wires on the sheet: Entrada[31:0] = in_1
endmodule

module Types (
  input  [31:0] in_1,
  output [5:0] out_2,
  output [4:0] out_3,
  output [4:0] out_4,
  output [4:0] out_5,
  output [4:0] out_6,
  output [5:0] out_7,
  output [5:0] out_8,
  output [4:0] out_9,
  output [4:0] out_10,
  output [15:0] out_11,
  output [5:0] out_12,
  output [25:0] out_13
);

  Type_I type_i_1 (.in_1(in_1), .out_5(out_8), .out_4(out_9), .out_3(out_10), .out_2(out_11));
  Type_J type_j_1 (.in_1(in_1), .out_3(out_12), .out_2(out_13));
  Type_R type_r_1 (
    .out_7(out_2), .out_4(out_5), .out_3(out_6), .out_5(out_4), .out_2(out_7), .in_1(in_1), .out_6(out_3));
endmodule

module CtrlUnity (
  input  [5:0] in_1,
  output RegDst,
  output ALUSrc,
  output MemToReg,
  output RegWrite,
  output MemRead,
  output MemWrite,
  output Branch,
  output ALUOp1,
  output ALUOp0
);

  and Format_R (ALUOp1, ~in_1[5], ~in_1[5], ~in_1[5], ~in_1[5], ~in_1[5], ~in_1[5]);  // AND_Gate
  and lw (MemRead, in_1[5], ~in_1[5], ~in_1[5], ~in_1[5], in_1[5], in_1[5]);  // AND_Gate
  and sw (MemWrite, in_1[5], ~in_1[5], in_1[5], ~in_1[5], in_1[5], in_1[5]);  // AND_Gate
  and beq (ALUOp0, ~in_1[5], ~in_1[5], ~in_1[5], in_1[5], ~in_1[5], ~in_1[5]);  // AND_Gate
  or or_1 (ALUSrc, MemRead, MemWrite);
  or or_2 (RegWrite, ALUOp1, MemRead);

  assign Branch = ALUOp0;
  assign in_1[4:0] = {5{in_1[5]}};
  assign MemToReg = MemRead;
  assign RegDst = ALUOp1;
endmodule

module ALUCtrl (
  input  [15:0] in_1,
  input  ALUOp1,
  input  ALUOp0,
  output [2:0] out_4
);

  wire and_1_out, or_1_out;

  or or_1 (or_1_out, in_1[3], in_1[0]);
  and and_1 (and_1_out, ALUOp1, in_1[1]);
  and and_2 (out_4[0], ALUOp1, or_1_out);
  or or_2 (out_4[2], ALUOp0, and_1_out);
  or or_3 (out_4[1], ~ALUOp1, ~in_1[2]);  // OR_Gate

  // Notes on the sheet:
  //   Descartados
endmodule

module ULA (
  input  [31:0] A,
  input  [31:0] B,
  input  [2:0] in_3,
  output out_4,
  output [31:0] out_5
);

  wire adder_1_cout, SComp;
  wire [31:0] S1, S2, S3, S4, S5;

  assign S1 = A & B;  // AND_Gate and_1, 32 bits wide
  assign S2 = A | B;  // OR_Gate or_1, 32 bits wide
  Adder #(.width(32)) adder_1 (.a(A), .b(B), .out(S3), .cout(adder_1_cout));  // open: cin
  Subtractor #(.width(32)) subtractor_1 (.a(A), .b(B), .out(S4), .bin(adder_1_cout));  // open: bout
  Comparator #(.width(32)) comparator_1 (.a(A), .b(B), .lt(SComp));  // open: gt, eq
  assign S5 = {{31{1'b0}}, SComp};  // Bit_Extender bit_extender_1
  Multiplexer #(.select(3), .width(32)) multiplexer_1 (
    .in0(S1), .in1(S2), .in2(S3), .in6(S4), .in7(S5), .out(out_5), .sel(in_3));  // open: in3, in4, in5, en
  nor nor_1 (out_4, out_5[0], out_5[1], out_5[2], out_5[3], out_5[4], out_5[5], out_5[6], out_5[7], out_5[8], out_5[9], out_5[10], out_5[11], out_5[12], out_5[13], out_5[14], out_5[15], out_5[16], out_5[17], out_5[18], out_5[19], out_5[20], out_5[21], out_5[22], out_5[23], out_5[24], out_5[25], out_5[26], out_5[27], out_5[28], out_5[29], out_5[30], out_5[31]);

  // Other names for the same wires on the sheet: Op[2:0] = in_3
endmodule

module MemData (
  input  [31:0] Addr,
  input  [31:0] DataIn,
  input  MemWrite,
  input  CLK,
  input  MemRead,
  output [31:0] DataOut
);

  RAM #(.addrWidth(24), .dataWidth(32), .bus("separate")) ram_1 (
    .addr(Addr[25:2]), .din(DataIn), .data(DataOut), .str(MemWrite), .clk(CLK), .ld(MemRead));  // open: sel, clr
endmodule

module Shift_Left_2 (
  input  [31:0] in_1,
  output [31:0] out_2
);


  assign out_2 = {in_1[29:0], 2'b00};
endmodule
